// Logisim project MultiCycleMips.circ as structural Verilog
module main (
);

  wire ALUSrcA, Branch, Clk, IRWrite, Jal, JR, lorD, MemRead, MemtoReg, MemWrite, or_1_out, PCWrite,
       PCWriteCond, RegDst, RegWrite, Zero;
  wire [1:0] ALUSrcB, PCSource;
  wire [2:0] ALUOp, ALUOp_hint;
  wire [3:0] Bit28_31;
  wire [4:0] WrAddr;
  wire [5:0] Bit0_5, Bit26_31;
  wire [7:0] multiplexer_1_out;
  wire [15:6] Bit0_15;
  wire [25:16] Bit0_25;
  wire [27:0] PC;
  wire [31:0] A, alu_1_aluresult, ALUOut, B, IR, MDRR, multiplexer_4_out, multiplexer_5_out, PCOut,
       regfile_1_rddata1, regfile_1_rddata2, shift_left2_1_output, signextend_1_output, WrData;

  Clock clock_1 (.out(Clk));
  or or_1 (or_1_out, Branch, PCWrite);
  Register #(.width(32)) u_PC (.D(PCOut), .en(or_1_out), .Q({Bit28_31, PC}), .clk(Clk));  // open: clr
  and and_1 (Branch, PCWriteCond, Zero);
  Multiplexer #(.width(8)) multiplexer_1 (
    .in0(PC[9:2]), .in1(ALUOut[7:0]), .out(multiplexer_1_out), .sel(lorD));  // open: en
  RAM #(.dataWidth(32), .bus("separate")) ram_1 (
    .addr(multiplexer_1_out), .din(B), .data(IR), .str(MemWrite), .clk(Clk), .ld(MemRead));  // open: sel, clr
  // Probe on IR
  // Probe on Bit26_31
  // Probe on Bit0_5
  // Probe on {Bit26_31, Bit0_25, Bit0_15, Bit0_5}
  Register #(.width(32)) u_IR (.D(IR), .en(IRWrite), .Q({Bit26_31, Bit0_25, Bit0_15, Bit0_5}), .clk(Clk));  // open: clr
  // Probe on PCSource
  Control_Unit control_unit_1 (
    .Opcode(Bit26_31), .func(Bit0_5), .Clock(Clk), .Jal(Jal), .PCSource(PCSource), .AluOp(ALUOp_hint),
    .ALUSrcB(ALUSrcB), .ALUSrcA(ALUSrcA), .RegWrite(RegWrite), .RegDst(RegDst), .IRWrite(IRWrite),
    .MemtoReg(MemtoReg), .MemWrite(MemWrite), .MemRead(MemRead), .IorD(lorD), .PCWrite(PCWrite),
    .PCWriteCond(PCWriteCond), .JR(JR));
  // Probe on ALUOp_hint
  // Probe on ALUSrcB
  // Probe on {Jal, MemtoReg}
  Multiplexer #(.select(2), .width(32), .enable("false")) multiplexer_2 (
    .in0(ALUOut), .in1(MDRR), .in2({Bit28_31, PC}), .in3({Bit28_31, PC}), .out(WrData), .sel({Jal, MemtoReg}));
  Multiplexer #(.select(2), .width(5), .enable("false")) multiplexer_3 (
    .in0(Bit0_25[20:16]), .in1(Bit0_15[15:11]), .in2({5{1'b1}}), .in3({5{1'b1}}), .out(WrAddr),
    .sel({Jal, RegDst}));
  RegFile regfile_1 (
    .WrAddr(WrAddr), .WrData(WrData), .WrReg(RegWrite), .RdAddr1(Bit0_25[25:21]), .RdAddr2(Bit0_25[20:16]),
    .RdData1(regfile_1_rddata1), .RdData2(regfile_1_rddata2), .Clock(Clk));
  Register #(.width(32)) MDR (.D(IR), .Q(MDRR), .clk(Clk));  // open: en, clr
  // Probe on regfile_1_rddata1
  // Probe on regfile_1_rddata2
  ALUcontrol alucontrol_1 (
    .H2(ALUOp_hint[2]), .H1(ALUOp_hint[1]), .H0(ALUOp_hint[0]), .F5(Bit0_5[5]), .F4(Bit0_5[4]),
    .F3(Bit0_5[3]), .F2(Bit0_5[2]), .F1(Bit0_5[1]), .F0(Bit0_5[0]), .ALU2(ALUOp[2]), .ALU1(ALUOp[1]),
    .ALU0(ALUOp[0]));
  Register #(.width(32)) u_A (.D(regfile_1_rddata1), .Q(A), .clk(Clk));  // open: en, clr
  Register #(.width(32)) u_B (.D(regfile_1_rddata2), .Q(B), .clk(Clk));  // open: en, clr
  SignExtend signextend_1 (.Output(signextend_1_output), .Input({Bit0_15, Bit0_5}));
  Shift_Left2 shift_left2_1 (.Input(signextend_1_output), .Output(shift_left2_1_output));
  Multiplexer #(.width(32), .enable("false")) multiplexer_4 (
    .in0({Bit28_31, PC}), .in1(A), .out(multiplexer_4_out), .sel(ALUSrcA));
  Multiplexer #(.select(2), .width(32), .enable("false")) multiplexer_5 (
    .in0(B), .in1(32'h4), .in2(signextend_1_output), .in3(shift_left2_1_output), .out(multiplexer_5_out),
    .sel(ALUSrcB));
  ALU alu_1 (
    .ALUCtl(ALUOp), .A(multiplexer_4_out), .B(multiplexer_5_out), .ALUResult(alu_1_aluresult), .Zero(Zero),
    .Shamt(Bit0_15[10:6]));  // open: Overflow
  // Probe on alu_1_aluresult
  Register #(.width(32)) u_ALUout (.D(alu_1_aluresult), .Q(ALUOut), .clk(Clk));  // open: en, clr
  Multiplexer #(.select(2), .width(32)) multiplexer_6 (
    .in0(alu_1_aluresult), .in1(ALUOut), .in2({Bit28_31, Bit0_25, Bit0_15, Bit0_5, 2'b00}), .in3(A),
    .out(PCOut), .sel(PCSource));  // open: en
  // Probe on PCOut
  // Probe on {Bit28_31, PC}
  // Probe on Branch
  // Probe on nothing
  // Probe on Jal
  // Probe on JR
  // Probe on RegWrite
  // Probe on WrAddr
  // Probe on WrData
  // Probe on MemWrite
  // Probe on B

  // Other names for the same wires on the sheet: Bit0_15[5:0] = Bit0_5; Bit0_25[15:0] = {Bit0_15, Bit0_5};
  //   shmt[4:0] = Bit0_15[10:6]; Bit11_15[4:0] = Bit0_15[15:11]; Bit16_20[4:0] = Bit0_25[20:16];
  //   Bit21_25[4:0] = Bit0_25[25:21]; PC[31:28] = Bit28_31; MDR[31:0] = IR

  // Notes on the sheet:
  //   We don't use Jump signal seperately
endmodule

module _32bit (
  input  Add_Sub_control,
  input  [31:0] in_2,
  input  [31:0] in_3,
  output [31:0] out_4,
  output carry_out
);

  wire adder_1_cout, subtractor_1_bout;
  wire [31:0] adder_1_out, subtractor_1_out;

  Adder #(.width(32)) adder_1 (.a(in_2), .b(in_3), .out(adder_1_out), .cout(adder_1_cout));  // open: cin
  Subtractor #(.width(32)) subtractor_1 (
    .a(in_2), .b(in_3), .out(subtractor_1_out), .bout(subtractor_1_bout));  // open: bin
  Multiplexer #(.width(32), .enable("false")) multiplexer_1 (
    .in0(adder_1_out), .in1(subtractor_1_out), .out(out_4), .sel(Add_Sub_control));
  Multiplexer #(.enable("false")) multiplexer_2 (
    .in0(adder_1_cout), .in1(subtractor_1_bout), .out(carry_out), .sel(Add_Sub_control));
endmodule

module ALU (
  input  [2:0] ALUCtl,
  input  [31:0] A,
  input  [31:0] B,
  input  [4:0] Shamt,
  output [31:0] ALUResult,
  output Zero,
  output Overflow
);

  wire and_2_out, and_3_out, comparator_1_lt, not_1_out, not_2_out, not_3_out, or_2_out;
  wire [31:0] Add, And, LessThan, Nor, Or, ShiftLeft, ShiftRight, Sub, Xor;

  // Probe on ALUCtl
  assign Nor = ~(A | B);  // NOR_Gate nor_1, 32 bits wide
  Adder #(.width(32)) adder_1 (.a(A), .b(B), .out(Add));  // open: cin, cout
  Subtractor #(.width(32)) subtractor_1 (.a(A), .b(B), .out(Sub));  // open: bin, bout
  assign And = A & B;  // AND_Gate and_1, 32 bits wide
  assign Or = A | B;  // OR_Gate or_1, 32 bits wide
  assign Xor = A ^ B;  // XOR_Gate xor_1, 32 bits wide
  Comparator #(.width(32)) comparator_1 (.a(A), .b(B), .lt(comparator_1_lt));  // open: gt, eq
  assign LessThan = {{31{1'b0}}, comparator_1_lt};  // Bit_Extender bit_extender_1
  Shifter #(.width(32)) shifter_1 (.in(B), .\dist (Shamt), .out(ShiftLeft));
  Shifter #(.width(32), .shift("lr")) shifter_2 (.in(B), .\dist (Shamt), .out(ShiftRight));
  not not_1 (not_1_out, ALUCtl[2]);
  Multiplexer #(.select(3), .width(32), .enable("false")) multiplexer_1 (
    .in0(LessThan), .in1(Sub), .in2(Nor), .in3(And), .in4(Add), .in5(Or), .in6(ShiftLeft), .in7(ShiftRight),
    .out(ALUResult), .sel(ALUCtl));
  not not_2 (not_2_out, ALUCtl[0]);
  not not_3 (not_3_out, ALUCtl[1]);
  and and_2 (and_2_out, not_2_out, not_3_out, ALUCtl[2]);
  and and_3 (and_3_out, not_2_out, ALUCtl[1], not_1_out);
  Overflow overflow_1 (
    .Add(and_2_out), .Sub(and_3_out), .ASign(A[31]), .BSign(B[31]), .ResultSign(ALUResult[31]),
    .Overflow(Overflow));
  or or_2 (or_2_out, ALUResult[0], ALUResult[1], ALUResult[2], ALUResult[3], ALUResult[4], ALUResult[5], ALUResult[6], ALUResult[7], ALUResult[8], ALUResult[9], ALUResult[10], ALUResult[11], ALUResult[12], ALUResult[13], ALUResult[14], ALUResult[15], ALUResult[16], ALUResult[17], ALUResult[18], ALUResult[19], ALUResult[20], ALUResult[21], ALUResult[22], ALUResult[23], ALUResult[24], ALUResult[25], ALUResult[26], ALUResult[27], ALUResult[28], ALUResult[29], ALUResult[30], ALUResult[31]);
  not not_4 (Zero, or_2_out);

  // Other names for the same wires on the sheet: ASign = A[31]; ResultSign = ALUResult[31]; BSign = B[31]
endmodule

module RegFile (
  input  [4:0] WrAddr,
  input  [31:0] WrData,
  input  WrReg,
  input  [4:0] RdAddr1,
  input  [4:0] RdAddr2,
  input  Clock,
  output [31:0] RdData1,
  output [31:0] RdData2
);

  wire WrReg0, WrReg1, WrReg2, WrReg3, WrReg4, WrReg5, WrReg6, WrReg7, WrReg8, WrReg9, WrReg10, WrReg11,
       WrReg12, WrReg13, WrReg14, WrReg15, WrReg16, WrReg17, WrReg18, WrReg19, WrReg20, WrReg21, WrReg22,
       WrReg23, WrReg24, WrReg25, WrReg26, WrReg27, WrReg28, WrReg29, WrReg30, WrReg31;
  wire [31:0] RegData1, RegData2, RegData3, RegData4, RegData5, RegData6, RegData7, RegData8, RegData9,
       RegData10, RegData11, RegData12, RegData13, RegData14, RegData15, RegData16, RegData17, RegData18,
       RegData19, RegData20, RegData21, RegData22, RegData23, RegData24, RegData25, RegData26, RegData27,
       RegData28, RegData29, RegData30, RegData31;

  Demultiplexer #(.select(5), .enable("false")) demultiplexer_1 (
    .out0(WrReg0), .out1(WrReg1), .out2(WrReg2), .out3(WrReg3), .out4(WrReg4), .out5(WrReg5), .out6(WrReg6),
    .out7(WrReg7), .out8(WrReg8), .out9(WrReg9), .out10(WrReg10), .out11(WrReg11), .out12(WrReg12),
    .out13(WrReg13), .out14(WrReg14), .out15(WrReg15), .out16(WrReg16), .out17(WrReg17), .out18(WrReg18),
    .out19(WrReg19), .out20(WrReg20), .out21(WrReg21), .out22(WrReg22), .out23(WrReg23), .out24(WrReg24),
    .out25(WrReg25), .out26(WrReg26), .out27(WrReg27), .out28(WrReg28), .out29(WrReg29), .out30(WrReg30),
    .out31(WrReg31), .in(WrReg), .sel(WrAddr));
  Register #(.width(32)) Reg4 (.D(WrData), .en(WrReg4), .Q(RegData4), .clk(Clock));  // open: clr
  Register #(.width(32)) Reg8 (.D(WrData), .en(WrReg8), .Q(RegData8), .clk(Clock));  // open: clr
  Register #(.width(32)) Reg12 (.D(WrData), .en(WrReg12), .Q(RegData12), .clk(Clock));  // open: clr
  Register #(.width(32)) Reg16 (.D(WrData), .en(WrReg16), .Q(RegData16), .clk(Clock));  // open: clr
  Register #(.width(32)) Reg20 (.D(WrData), .en(WrReg20), .Q(RegData20), .clk(Clock));  // open: clr
  Register #(.width(32)) Reg24 (.D(WrData), .en(WrReg24), .Q(RegData24), .clk(Clock));  // open: clr
  Register #(.width(32)) Reg28 (.D(WrData), .en(WrReg28), .Q(RegData28), .clk(Clock));  // open: clr
  Register #(.width(32)) Reg1 (.D(WrData), .en(WrReg1), .Q(RegData1), .clk(Clock));  // open: clr
  Register #(.width(32)) Reg5 (.D(WrData), .en(WrReg5), .Q(RegData5), .clk(Clock));  // open: clr
  Register #(.width(32)) Reg9 (.D(WrData), .en(WrReg9), .Q(RegData9), .clk(Clock));  // open: clr
  Register #(.width(32)) Reg13 (.D(WrData), .en(WrReg13), .Q(RegData13), .clk(Clock));  // open: clr
  Register #(.width(32)) Reg17 (.D(WrData), .en(WrReg17), .Q(RegData17), .clk(Clock));  // open: clr
  Register #(.width(32)) Reg21 (.D(WrData), .en(WrReg21), .Q(RegData21), .clk(Clock));  // open: clr
  Register #(.width(32)) Reg25 (.D(WrData), .en(WrReg25), .Q(RegData25), .clk(Clock));  // open: clr
  Register #(.width(32)) Reg29 (.D(WrData), .en(WrReg29), .Q(RegData29), .clk(Clock));  // open: clr
  Register #(.width(32)) Reg2 (.D(WrData), .en(WrReg2), .Q(RegData2), .clk(Clock));  // open: clr
  Register #(.width(32)) Reg6 (.D(WrData), .en(WrReg6), .Q(RegData6), .clk(Clock));  // open: clr
  Register #(.width(32)) Reg10 (.D(WrData), .en(WrReg10), .Q(RegData10), .clk(Clock));  // open: clr
  Register #(.width(32)) Reg14 (.D(WrData), .en(WrReg14), .Q(RegData14), .clk(Clock));  // open: clr
  Register #(.width(32)) Reg18 (.D(WrData), .en(WrReg18), .Q(RegData18), .clk(Clock));  // open: clr
  Register #(.width(32)) Reg22 (.D(WrData), .en(WrReg22), .Q(RegData22), .clk(Clock));  // open: clr
  Register #(.width(32)) Reg26 (.D(WrData), .en(WrReg26), .Q(RegData26), .clk(Clock));  // open: clr
  Register #(.width(32)) Reg30 (.D(WrData), .en(WrReg30), .Q(RegData30), .clk(Clock));  // open: clr
  Register #(.width(32)) Reg3 (.D(WrData), .en(WrReg3), .Q(RegData3), .clk(Clock));  // open: clr
  Register #(.width(32)) Reg7 (.D(WrData), .en(WrReg7), .Q(RegData7), .clk(Clock));  // open: clr
  Register #(.width(32)) Reg11 (.D(WrData), .en(WrReg11), .Q(RegData11), .clk(Clock));  // open: clr
  Register #(.width(32)) Reg15 (.D(WrData), .en(WrReg15), .Q(RegData15), .clk(Clock));  // open: clr
  Register #(.width(32)) Reg19 (.D(WrData), .en(WrReg19), .Q(RegData19), .clk(Clock));  // open: clr
  Register #(.width(32)) Reg23 (.D(WrData), .en(WrReg23), .Q(RegData23), .clk(Clock));  // open: clr
  Register #(.width(32)) Reg27 (.D(WrData), .en(WrReg27), .Q(RegData27), .clk(Clock));  // open: clr
  Register #(.width(32)) Reg31 (.D(WrData), .en(WrReg31), .Q(RegData31), .clk(Clock));  // open: clr
  Multiplexer #(.select(5), .width(32), .enable("false")) multiplexer_1 (
    .in0({32{1'b0}}), .in1(RegData1), .in2(RegData2), .in3(RegData3), .in4(RegData4), .in5(RegData5),
    .in6(RegData6), .in7(RegData7), .in8(RegData8), .in9(RegData9), .in10(RegData10), .in11(RegData11),
    .in12(RegData12), .in13(RegData13), .in14(RegData14), .in15(RegData15), .in16(RegData16),
    .in17(RegData17), .in18(RegData18), .in19(RegData19), .in20(RegData20), .in21(RegData21),
    .in22(RegData22), .in23(RegData23), .in24(RegData24), .in25(RegData25), .in26(RegData26),
    .in27(RegData27), .in28(RegData28), .in29(RegData29), .in30(RegData30), .in31(RegData31), .out(RdData1),
    .sel(RdAddr1));
  Multiplexer #(.select(5), .width(32), .enable("false")) multiplexer_2 (
    .in0({32{1'b0}}), .in1(RegData1), .in2(RegData2), .in3(RegData3), .in4(RegData4), .in5(RegData5),
    .in6(RegData6), .in7(RegData7), .in8(RegData8), .in9(RegData9), .in10(RegData10), .in11(RegData11),
    .in12(RegData12), .in13(RegData13), .in14(RegData14), .in15(RegData15), .in16(RegData16),
    .in17(RegData17), .in18(RegData18), .in19(RegData19), .in20(RegData20), .in21(RegData21),
    .in22(RegData22), .in23(RegData23), .in24(RegData24), .in25(RegData25), .in26(RegData26),
    .in27(RegData27), .in28(RegData28), .in29(RegData29), .in30(RegData30), .in31(RegData31), .out(RdData2),
    .sel(RdAddr2));
endmodule

module Overflow (
  input  Add,
  input  Sub,
  input  ASign,
  input  BSign,
  input  ResultSign,
  output Overflow
);

  wire and_1_out, and_2_out, or_1_out, xnor_1_out, xor_1_out, xor_2_out;

  xnor xnor_1 (xnor_1_out, ASign, BSign);
  xor xor_1 (xor_1_out, ASign, BSign);
  and and_1 (and_1_out, xnor_1_out, Add);
  and and_2 (and_2_out, xor_1_out, Sub);
  or or_1 (or_1_out, and_1_out, and_2_out);
  xor xor_2 (xor_2_out, ResultSign, ASign);
  and and_3 (Overflow, or_1_out, xor_2_out);

  // Notes on the sheet:
  //   Overflow occurs when doing addition and sign(A) == sign(B) && sign(result) != sign(A)
  //   Or
  //   Overflow occurs when doing subtraction and sign(A) != sign(B) && sign(result) != sign(A)
endmodule

// MAIN_CONTROL
module Control_Unit (
  input  [5:0] Opcode,
  input  [5:0] func,
  input  Clock,
  output Jal,
  output [1:0] PCSource,
  output [2:0] AluOp,
  output [1:0] ALUSrcB,
  output ALUSrcA,
  output RegWrite,
  output RegDst,
  output IRWrite,
  output MemtoReg,
  output MemWrite,
  output MemRead,
  output IorD,
  output PCWrite,
  output PCWriteCond,
  output JR
);

  wire not_1_out, not_2_out, not_3_out, not_4_out, not_5_out, not_6_out, not_7_out;
  wire [2:0] currentState, NextState;
  wire [8:3] register_1_q;
  wire [20:0] rom_1_data;

  not not_1 (not_1_out, currentState[0]);
  not not_2 (not_2_out, currentState[2]);
  Register #(.width(9)) register_1 (
    .D({Opcode, NextState}), .Q({register_1_q, currentState}), .clk(Clock));  // open: en, clr
  not not_3 (not_3_out, func[5]);
  not not_4 (not_4_out, func[4]);
  not not_5 (not_5_out, func[2]);
  and and_1 (JR, not_3_out, not_4_out, func[3], not_5_out, not_6_out, not_7_out, not_1_out, currentState[1], not_2_out);
  not not_6 (not_6_out, func[1]);
  not not_7 (not_7_out, func[0]);
  ROM #(.addrWidth(9), .dataWidth(21)) rom_1 (.addr({register_1_q, currentState}), .data(rom_1_data));  // open: sel
  Multiplexer #(.width(21), .enable("false")) multiplexer_1 (
    .in0(rom_1_data), .in1(21'h18002),
    .out({Jal, NextState, PCSource, AluOp, ALUSrcB, ALUSrcA, RegWrite, RegDst, IRWrite, MemtoReg, MemWrite, MemRead, IorD, PCWrite, PCWriteCond}),
    .sel(JR));

  // Other names for the same wires on the sheet: Clk = Clock

  // Notes on the sheet:
  //   contents of rom_1 (hex, n*v repeats v):
  //   2044a 40c00 64200 4180 12*0 2044a 40c00 10002 5*0 2044a 40c00 110102 5*0 2044a 40c00 9201 29*0 2044a
  //   40c00 60a00 100 28*0 2044a 40c00 62a00 2100 4*0 2044a 40c00 63a00 3100 172*0 2044a 40c00 60a00 8000c
  //   120 59*0 2044a 40c00 60a00 14
endmodule

// ALU_CONTROL
module ALUcontrol (
  input  H2,
  input  H1,
  input  H0,
  input  F5,
  input  F4,
  input  F3,
  input  F2,
  input  F1,
  input  F0,
  output ALU2,
  output ALU1,
  output ALU0
);

  wire and_1_out, and_2_out, and_3_out, and_4_out, and_5_out, and_6_out, and_7_out, and_8_out, and_9_out,
       and_10_out, and_11_out, and_12_out, and_13_out, not_1_out, not_2_out, not_3_out, not_4_out, not_5_out,
       not_6_out, not_7_out, not_8_out, not_9_out, not_10_out, not_11_out, not_12_out, not_13_out,
       not_14_out, not_15_out, not_16_out, not_17_out;

  not not_1 (not_1_out, H2);
  not not_2 (not_2_out, H1);
  not not_3 (not_3_out, H0);
  not not_4 (not_4_out, H2);
  not not_5 (not_5_out, F5);
  not not_6 (not_6_out, F2);
  not not_7 (not_7_out, F1);
  not not_8 (not_8_out, F1);
  not not_9 (not_9_out, H2);
  not not_10 (not_10_out, H0);
  not not_11 (not_11_out, F5);
  not not_12 (not_12_out, F0);
  not not_13 (not_13_out, H2);
  not not_14 (not_14_out, H2);
  not not_15 (not_15_out, F3);
  not not_16 (not_16_out, F2);
  not not_17 (not_17_out, F1);
  and and_1 (and_1_out, not_1_out, not_2_out, not_3_out);
  and and_2 (and_2_out, not_4_out, H1, H0);
  and and_3 (and_3_out, H2, not_5_out);
  and and_4 (and_4_out, H2, not_6_out, not_7_out);
  and and_5 (and_5_out, H2, not_8_out, F0);
  and and_6 (and_6_out, not_9_out, H1, not_10_out);
  and and_7 (and_7_out, H2, not_11_out);
  and and_8 (and_8_out, H2, F2, not_12_out);
  and and_9 (and_9_out, H2, F2, F1);
  and and_10 (and_10_out, not_13_out, H0);
  and and_11 (and_11_out, not_14_out, H1);
  and and_12 (and_12_out, H2, not_15_out, not_16_out, F1);
  and and_13 (and_13_out, H2, F2, not_17_out);
  or or_1 (ALU2, and_1_out, and_2_out, and_3_out, and_4_out, and_5_out);
  or or_2 (ALU1, and_6_out, and_7_out, and_8_out, and_9_out);
  or or_3 (ALU0, and_10_out, and_11_out, and_12_out, and_13_out);
endmodule

module SignExtend (
  input  [15:0] Input,
  output [31:0] Output
);


  assign Output = {{17{Input[15]}}, Input[14:0]};
endmodule

// Shift Left2
module Shift_Left2 (
  input  [31:0] Input,
  output [31:0] Output
);

  Shifter #(.width(32)) shifter_1 (.in(Input), .\dist (5'b00010), .out(Output));

  // Notes on the sheet:
  //   Shift by 2 Bits only
endmodule
