// Logisim project SingleCycle.circ as structural Verilog: 9 circuits, main circuit RegFile
module main (
);

  wire ALU0, ALU1, ALU2, alu_1_p5, alu_1_p7, ALUSrc, Branch, clock, Jal, Jr, Jump, MemRead, MemToReg,
       MemWrite, PCSrc, RegDest, RegWrite;
  wire [4:0] multiplexer_2_out, WrADDr;
  wire [5:0] Bit0_5, Bit26_31;
  wire [15:6] Bit0_15;
  wire [25:16] Bit0_25;
  wire [31:0] adder_2_out, alu_1_p6, Data, Jal_value, MemData, multiplexer_1_out, multiplexer_4_out,
       multiplexer_5_out, multiplexer_7_out, PC, PC_in, RdData1, RdData2, shift_left2_1_output,
       signextend_1_output;

  Clock clock_1 (.out(clock));
  // Probe on multiplexer_1_out
  Multiplexer #(.width(32), .enable("false")) multiplexer_1 (
    .in0(PC_in), .in1(RdData1), .out(multiplexer_1_out), .sel(Jr));
  Register #(.width(32)) u_PC (.D(multiplexer_1_out), .Q(PC), .clk(clock));  // open: en, clr
  Control_Unit control_unit_1 (
    .I31(Bit26_31[5]), .I30(Bit26_31[4]), .I29(Bit26_31[3]), .I28(Bit26_31[2]), .I27(Bit26_31[1]),
    .I26(Bit26_31[0]), .I5(Bit0_5[5]), .I4(Bit0_5[4]), .I3(Bit0_5[3]), .I2(Bit0_5[2]), .I1(Bit0_5[1]),
    .I0(Bit0_5[0]), .ALU2(ALU2), .ALU1(ALU1), .ALU0(ALU0), .RegDst(RegDest), .Jump(Jump), .Branch(Branch),
    .MemRead(MemRead), .MemToReg(MemToReg), .MemWrite(MemWrite), .ALUSrc(ALUSrc), .RegWrite(RegWrite),
    .Jr(Jr), .Jal(Jal));
  Multiplexer #(.width(5)) multiplexer_2 (
    .in0(Bit0_25[20:16]), .in1(Bit0_15[15:11]), .out(multiplexer_2_out), .sel(RegDest));  // open: en
  Multiplexer #(.width(5), .enable("false")) multiplexer_3 (
    .in0(multiplexer_2_out), .in1({5{1'b1}}), .out(WrADDr), .sel(Jal));
  // Probe on Data
  // Probe on WrADDr
  ROM #(.dataWidth(32)) rom_1 (.addr(PC[9:2]), .data({Bit26_31, Bit0_25, Bit0_15, Bit0_5}));  // open: sel
  RegFile regfile_1 (
    .WrAddr(WrADDr), .WrData(Data), .WrReg(RegWrite), .RdAddr1(Bit0_25[25:21]), .RdAddr2(Bit0_25[20:16]),
    .RdData1(RdData1), .RdData2(RdData2), .Clock(clock));
  // Probe on PC
  // Probe on RdData2
  SignExtend signextend_1 (.Input({Bit0_15, Bit0_5}), .Output(signextend_1_output));
  Adder #(.width(32)) adder_1 (.a(PC), .b(32'h4), .out(Jal_value));  // open: cin, cout
  Shift_Left2 shift_left2_1 (.Input(signextend_1_output), .Output(shift_left2_1_output));
  // Probe on RdData1
  Multiplexer #(.width(32)) multiplexer_4 (
    .in0(RdData2), .in1(signextend_1_output), .out(multiplexer_4_out), .sel(ALUSrc));  // open: en
  // Probe on signextend_1_output
  Adder #(.width(32)) adder_2 (.a(Jal_value), .b(shift_left2_1_output), .out(adder_2_out));  // open: cin, cout
  // ALU alu_1: pin names not known; wires that end beside it: RdData1, multiplexer_4_out, {5{1'b0}}, {ALU2, ALU1, ALU0}, alu_1_p5, alu_1_p6, alu_1_p7
  // Probe on {PC[31:28], Bit0_25, Bit0_15, Bit0_5, 2'b00}
  Multiplexer #(.width(32)) multiplexer_5 (
    .in0(Jal_value), .in1(adder_2_out), .out(multiplexer_5_out), .sel(PCSrc));  // open: en
  Multiplexer #(.width(32)) multiplexer_6 (
    .in0(multiplexer_5_out), .in1({PC[31:28], Bit0_25, Bit0_15, Bit0_5, 2'b00}), .out(PC_in), .sel(Jump));  // open: en
  and and_1 (PCSrc, Branch, alu_1_p5);
  // Probe on alu_1_p6
  RAM #(.dataWidth(32), .bus("separate")) ram_1 (
    .addr(alu_1_p6[7:0]), .din(RdData2), .data(MemData), .str(MemWrite), .clk(clock), .ld(MemRead));  // open: sel, clr
  // Probe on PC
  // Probe on Branch
  // Probe on Jump
  // Probe on Jal
  // Probe on Jr
  // Probe on RegWrite
  // Probe on WrADDr
  // Probe on Data
  // Probe on MemWrite
  // Probe on RdData2
  Multiplexer #(.width(32)) multiplexer_7 (
    .in0(alu_1_p6), .in1(MemData), .out(multiplexer_7_out), .sel(MemToReg));  // open: en
  Multiplexer #(.width(32), .enable("false")) multiplexer_8 (
    .in0(multiplexer_7_out), .in1(Jal_value), .out(Data), .sel(Jal));

  // Other names for the same wires on the sheet: Bit0_15[5:0] = Bit0_5; Bit0_25[15:0] = {Bit0_15, Bit0_5};
  //   Bit11_15[4:0] = Bit0_15[15:11]; Bit16_20[4:0] = Bit0_25[20:16]; Bit21_25[4:0] = Bit0_25[25:21]

  // Notes on the sheet:
  //   NOTE:
  //   Only Instruction 2-8 taken
  //   contents of rom_1 (hex, n*v repeats v):
  //   20010008 34220005 3043ffff 612020 832822 223024 c33825 aca40064 8ca80064 22482a 225027 11050003
  //   1034022 c00000b 200b0001 200c0005
  //   Data memory
endmodule

module _32bit (
  input  Add_Sub_control,
  input  [31:0] in_2,
  input  [31:0] in_3,
  output [31:0] out_4,
  output carry_out
);

  wire adder_1_cout, subtractor_1_bout;
  wire [31:0] adder_1_out, subtractor_1_out;

  Adder #(.width(32)) adder_1 (.a(in_2), .b(in_3), .out(adder_1_out), .cout(adder_1_cout));  // open: cin
  Subtractor #(.width(32)) subtractor_1 (
    .a(in_2), .b(in_3), .out(subtractor_1_out), .bout(subtractor_1_bout));  // open: bin
  Multiplexer #(.width(32), .enable("false")) multiplexer_1 (
    .in0(adder_1_out), .in1(subtractor_1_out), .out(out_4), .sel(Add_Sub_control));
  Multiplexer #(.enable("false")) multiplexer_2 (
    .in0(adder_1_cout), .in1(subtractor_1_bout), .out(carry_out), .sel(Add_Sub_control));
endmodule

module ALU (
  input  [2:0] ALUCtl,
  input  [31:0] A,
  input  [31:0] B,
  input  [4:0] Shamt,
  output [31:0] ALUResult,
  output Zero,
  output Overflow
);

  wire and_2_out, and_3_out, comparator_1_lt, not_1_out, not_2_out, not_3_out, or_2_out;
  wire [31:0] Add, And, LessThan, Nor, Or, ShiftLeft, ShiftRight, Sub, Xor;

  // Probe on ALUCtl
  assign Nor = ~(A | B);  // NOR_Gate nor_1, 32 bits wide
  Adder #(.width(32)) adder_1 (.a(A), .b(B), .out(Add));  // open: cin, cout
  Subtractor #(.width(32)) subtractor_1 (.a(A), .b(B), .out(Sub));  // open: bin, bout
  assign And = A & B;  // AND_Gate and_1, 32 bits wide
  assign Or = A | B;  // OR_Gate or_1, 32 bits wide
  assign Xor = A ^ B;  // XOR_Gate xor_1, 32 bits wide
  Comparator #(.width(32)) comparator_1 (.a(A), .b(B), .lt(comparator_1_lt));  // open: gt, eq
  assign LessThan = {{31{1'b0}}, comparator_1_lt};  // Bit_Extender bit_extender_1
  Shifter #(.width(32)) shifter_1 (.in(B), .\dist (Shamt), .out(ShiftLeft));
  Shifter #(.width(32), .shift("lr")) shifter_2 (.in(B), .\dist (Shamt), .out(ShiftRight));
  not not_1 (not_1_out, ALUCtl[2]);
  Multiplexer #(.select(3), .width(32), .enable("false")) multiplexer_1 (
    .in0(LessThan), .in1(Sub), .in2(Nor), .in3(And), .in4(Add), .in5(Or), .in6(ShiftLeft), .in7(ShiftRight),
    .out(ALUResult), .sel(ALUCtl));
  not not_2 (not_2_out, ALUCtl[0]);
  not not_3 (not_3_out, ALUCtl[1]);
  and and_2 (and_2_out, not_2_out, not_3_out, ALUCtl[2]);
  and and_3 (and_3_out, not_2_out, ALUCtl[1], not_1_out);
  Overflow overflow_1 (
    .Add(and_2_out), .Sub(and_3_out), .ASign(A[31]), .BSign(B[31]), .ResultSign(ALUResult[31]),
    .Overflow(Overflow));
  or or_2 (or_2_out, ALUResult[0], ALUResult[1], ALUResult[2], ALUResult[3], ALUResult[4], ALUResult[5], ALUResult[6], ALUResult[7], ALUResult[8], ALUResult[9], ALUResult[10], ALUResult[11], ALUResult[12], ALUResult[13], ALUResult[14], ALUResult[15], ALUResult[16], ALUResult[17], ALUResult[18], ALUResult[19], ALUResult[20], ALUResult[21], ALUResult[22], ALUResult[23], ALUResult[24], ALUResult[25], ALUResult[26], ALUResult[27], ALUResult[28], ALUResult[29], ALUResult[30], ALUResult[31]);
  not not_4 (Zero, or_2_out);

  // Other names for the same wires on the sheet: ASign = A[31]; ResultSign = ALUResult[31]; BSign = B[31]
endmodule

module RegFile (
  input  [4:0] WrAddr,
  input  [31:0] WrData,
  input  WrReg,
  input  [4:0] RdAddr1,
  input  [4:0] RdAddr2,
  input  Clock,
  output [31:0] RdData1,
  output [31:0] RdData2
);

  wire WrReg0, WrReg1, WrReg2, WrReg3, WrReg4, WrReg5, WrReg6, WrReg7, WrReg8, WrReg9, WrReg10, WrReg11,
       WrReg12, WrReg13, WrReg14, WrReg15, WrReg16, WrReg17, WrReg18, WrReg19, WrReg20, WrReg21, WrReg22,
       WrReg23, WrReg24, WrReg25, WrReg26, WrReg27, WrReg28, WrReg29, WrReg30, WrReg31;
  wire [31:0] RegData1, RegData2, RegData3, RegData4, RegData5, RegData6, RegData7, RegData8, RegData9,
       RegData10, RegData11, RegData12, RegData13, RegData14, RegData15, RegData16, RegData17, RegData18,
       RegData19, RegData20, RegData21, RegData22, RegData23, RegData24, RegData25, RegData26, RegData27,
       RegData28, RegData29, RegData30, RegData31;

  Demultiplexer #(.select(5), .enable("false")) demultiplexer_1 (
    .out0(WrReg0), .out1(WrReg1), .out2(WrReg2), .out3(WrReg3), .out4(WrReg4), .out5(WrReg5), .out6(WrReg6),
    .out7(WrReg7), .out8(WrReg8), .out9(WrReg9), .out10(WrReg10), .out11(WrReg11), .out12(WrReg12),
    .out13(WrReg13), .out14(WrReg14), .out15(WrReg15), .out16(WrReg16), .out17(WrReg17), .out18(WrReg18),
    .out19(WrReg19), .out20(WrReg20), .out21(WrReg21), .out22(WrReg22), .out23(WrReg23), .out24(WrReg24),
    .out25(WrReg25), .out26(WrReg26), .out27(WrReg27), .out28(WrReg28), .out29(WrReg29), .out30(WrReg30),
    .out31(WrReg31), .in(WrReg), .sel(WrAddr));
  Register #(.width(32)) Reg4 (.D(WrData), .en(WrReg4), .Q(RegData4), .clk(Clock));  // open: clr
  Register #(.width(32)) Reg8 (.D(WrData), .en(WrReg8), .Q(RegData8), .clk(Clock));  // open: clr
  Register #(.width(32)) Reg12 (.D(WrData), .en(WrReg12), .Q(RegData12), .clk(Clock));  // open: clr
  Register #(.width(32)) Reg16 (.D(WrData), .en(WrReg16), .Q(RegData16), .clk(Clock));  // open: clr
  Register #(.width(32)) Reg20 (.D(WrData), .en(WrReg20), .Q(RegData20), .clk(Clock));  // open: clr
  Register #(.width(32)) Reg24 (.D(WrData), .en(WrReg24), .Q(RegData24), .clk(Clock));  // open: clr
  Register #(.width(32)) Reg28 (.D(WrData), .en(WrReg28), .Q(RegData28), .clk(Clock));  // open: clr
  Register #(.width(32)) Reg1 (.D(WrData), .en(WrReg1), .Q(RegData1), .clk(Clock));  // open: clr
  Register #(.width(32)) Reg5 (.D(WrData), .en(WrReg5), .Q(RegData5), .clk(Clock));  // open: clr
  Register #(.width(32)) Reg9 (.D(WrData), .en(WrReg9), .Q(RegData9), .clk(Clock));  // open: clr
  Register #(.width(32)) Reg13 (.D(WrData), .en(WrReg13), .Q(RegData13), .clk(Clock));  // open: clr
  Register #(.width(32)) Reg17 (.D(WrData), .en(WrReg17), .Q(RegData17), .clk(Clock));  // open: clr
  Register #(.width(32)) Reg21 (.D(WrData), .en(WrReg21), .Q(RegData21), .clk(Clock));  // open: clr
  Register #(.width(32)) Reg25 (.D(WrData), .en(WrReg25), .Q(RegData25), .clk(Clock));  // open: clr
  Register #(.width(32)) Reg29 (.D(WrData), .en(WrReg29), .Q(RegData29), .clk(Clock));  // open: clr
  Register #(.width(32)) Reg2 (.D(WrData), .en(WrReg2), .Q(RegData2), .clk(Clock));  // open: clr
  Register #(.width(32)) Reg6 (.D(WrData), .en(WrReg6), .Q(RegData6), .clk(Clock));  // open: clr
  Register #(.width(32)) Reg10 (.D(WrData), .en(WrReg10), .Q(RegData10), .clk(Clock));  // open: clr
  Register #(.width(32)) Reg14 (.D(WrData), .en(WrReg14), .Q(RegData14), .clk(Clock));  // open: clr
  Register #(.width(32)) Reg18 (.D(WrData), .en(WrReg18), .Q(RegData18), .clk(Clock));  // open: clr
  Register #(.width(32)) Reg22 (.D(WrData), .en(WrReg22), .Q(RegData22), .clk(Clock));  // open: clr
  Register #(.width(32)) Reg26 (.D(WrData), .en(WrReg26), .Q(RegData26), .clk(Clock));  // open: clr
  Register #(.width(32)) Reg30 (.D(WrData), .en(WrReg30), .Q(RegData30), .clk(Clock));  // open: clr
  Register #(.width(32)) Reg3 (.D(WrData), .en(WrReg3), .Q(RegData3), .clk(Clock));  // open: clr
  Register #(.width(32)) Reg7 (.D(WrData), .en(WrReg7), .Q(RegData7), .clk(Clock));  // open: clr
  Register #(.width(32)) Reg11 (.D(WrData), .en(WrReg11), .Q(RegData11), .clk(Clock));  // open: clr
  Register #(.width(32)) Reg15 (.D(WrData), .en(WrReg15), .Q(RegData15), .clk(Clock));  // open: clr
  Register #(.width(32)) Reg19 (.D(WrData), .en(WrReg19), .Q(RegData19), .clk(Clock));  // open: clr
  Register #(.width(32)) Reg23 (.D(WrData), .en(WrReg23), .Q(RegData23), .clk(Clock));  // open: clr
  Register #(.width(32)) Reg27 (.D(WrData), .en(WrReg27), .Q(RegData27), .clk(Clock));  // open: clr
  Register #(.width(32)) Reg31 (.D(WrData), .en(WrReg31), .Q(RegData31), .clk(Clock));  // open: clr
  Multiplexer #(.select(5), .width(32), .enable("false")) multiplexer_1 (
    .in0({32{1'b0}}), .in1(RegData1), .in2(RegData2), .in3(RegData3), .in4(RegData4), .in5(RegData5),
    .in6(RegData6), .in7(RegData7), .in8(RegData8), .in9(RegData9), .in10(RegData10), .in11(RegData11),
    .in12(RegData12), .in13(RegData13), .in14(RegData14), .in15(RegData15), .in16(RegData16),
    .in17(RegData17), .in18(RegData18), .in19(RegData19), .in20(RegData20), .in21(RegData21),
    .in22(RegData22), .in23(RegData23), .in24(RegData24), .in25(RegData25), .in26(RegData26),
    .in27(RegData27), .in28(RegData28), .in29(RegData29), .in30(RegData30), .in31(RegData31), .out(RdData1),
    .sel(RdAddr1));
  Multiplexer #(.select(5), .width(32), .enable("false")) multiplexer_2 (
    .in0({32{1'b0}}), .in1(RegData1), .in2(RegData2), .in3(RegData3), .in4(RegData4), .in5(RegData5),
    .in6(RegData6), .in7(RegData7), .in8(RegData8), .in9(RegData9), .in10(RegData10), .in11(RegData11),
    .in12(RegData12), .in13(RegData13), .in14(RegData14), .in15(RegData15), .in16(RegData16),
    .in17(RegData17), .in18(RegData18), .in19(RegData19), .in20(RegData20), .in21(RegData21),
    .in22(RegData22), .in23(RegData23), .in24(RegData24), .in25(RegData25), .in26(RegData26),
    .in27(RegData27), .in28(RegData28), .in29(RegData29), .in30(RegData30), .in31(RegData31), .out(RdData2),
    .sel(RdAddr2));
endmodule

module Overflow (
  input  Add,
  input  Sub,
  input  ASign,
  input  BSign,
  input  ResultSign,
  output Overflow
);

  wire and_1_out, and_2_out, or_1_out, xnor_1_out, xor_1_out, xor_2_out;

  xnor xnor_1 (xnor_1_out, ASign, BSign);
  xor xor_1 (xor_1_out, ASign, BSign);
  and and_1 (and_1_out, xnor_1_out, Add);
  and and_2 (and_2_out, xor_1_out, Sub);
  or or_1 (or_1_out, and_1_out, and_2_out);
  xor xor_2 (xor_2_out, ResultSign, ASign);
  and and_3 (Overflow, or_1_out, xor_2_out);

  // Notes on the sheet:
  //   Overflow occurs when doing addition and sign(A) == sign(B) && sign(result) != sign(A)
  //   Or
  //   Overflow occurs when doing subtraction and sign(A) != sign(B) && sign(result) != sign(A)
endmodule

module SignExtend (
  input  [15:0] Input,
  output [31:0] Output
);


  assign Output = {{17{Input[15]}}, Input[14:0]};
endmodule

// Shift Left2
module Shift_Left2 (
  input  [31:0] Input,
  output [31:0] Output
);

  Shifter #(.width(32)) shifter_1 (.in(Input), .\dist (5'b00010), .out(Output));

  // Notes on the sheet:
  //   Shift by 2 Bits only
endmodule

module Add (
  input  [31:0] A,
  input  [31:0] B,
  output [31:0] Output,
  output Overflow
);

  ALU alu_1 (.ALUCtl(3'b100), .A(A), .B(B), .ALUResult(Output), .Overflow(Overflow), .Shamt({5{1'b0}}));  // open: Zero

  // Notes on the sheet:
  //   ADD function: 101
endmodule

module Control_Unit (
  input  I31,
  input  I30,
  input  I29,
  input  I28,
  input  I27,
  input  I26,
  input  I5,
  input  I4,
  input  I3,
  input  I2,
  input  I1,
  input  I0,
  output ALU2,
  output ALU1,
  output ALU0,
  output RegDst,
  output Jump,
  output Branch,
  output MemRead,
  output MemToReg,
  output MemWrite,
  output ALUSrc,
  output RegWrite,
  output Jr,
  output Jal
);

  wire and_1_out, and_2_out, and_3_out, and_4_out, and_5_out, and_6_out, and_7_out, and_8_out, and_9_out,
       and_10_out, and_11_out, and_12_out, and_13_out, and_14_out, and_15_out, and_16_out, and_17_out,
       and_23_out, and_24_out, and_25_out, and_26_out, and_27_out, and_28_out, and_29_out, and_30_out,
       and_31_out, and_32_out, and_33_out, and_34_out, and_35_out, and_36_out, not_1_out, not_2_out,
       not_3_out, not_4_out, not_5_out, not_6_out, not_7_out, not_8_out, not_9_out, not_10_out, not_11_out,
       not_12_out, not_13_out, not_14_out, not_15_out, not_16_out, not_17_out, not_18_out, not_19_out,
       not_20_out, not_21_out, not_22_out, not_23_out, not_24_out, not_25_out, not_26_out, not_27_out,
       not_28_out, not_29_out, not_30_out, not_31_out, not_32_out, not_33_out, not_34_out, not_35_out,
       not_36_out, not_37_out, not_38_out, not_39_out, not_40_out, not_41_out, not_42_out, not_43_out,
       not_44_out, not_45_out, not_46_out, not_47_out, not_48_out, not_49_out, not_50_out, not_51_out,
       not_52_out, not_53_out, not_54_out, not_55_out, not_56_out, not_57_out, not_58_out, not_59_out,
       not_60_out, not_61_out, not_62_out, not_63_out, not_64_out, not_65_out, not_66_out, not_67_out,
       not_68_out, not_69_out, not_70_out, not_71_out, not_72_out, not_73_out, not_74_out, not_75_out,
       not_76_out, not_77_out, not_78_out, not_79_out, not_80_out, not_81_out, not_82_out, not_83_out,
       not_84_out, not_85_out, not_86_out, not_87_out, not_88_out, not_89_out, not_90_out, not_91_out,
       not_92_out, not_93_out, not_94_out, not_95_out, not_96_out, not_97_out, not_98_out, not_99_out,
       not_100_out, not_101_out, not_102_out, not_103_out, not_104_out, not_105_out, not_106_out,
       not_107_out, not_108_out, not_109_out, not_110_out, not_111_out, not_112_out, not_113_out,
       not_114_out, not_115_out, not_116_out, not_117_out, not_118_out, not_119_out, not_120_out,
       not_121_out, not_122_out, not_123_out, not_124_out, not_125_out, not_126_out, not_127_out,
       not_128_out, not_129_out, not_130_out, not_131_out, not_132_out, not_133_out, not_134_out,
       not_135_out, not_136_out, not_137_out, not_138_out, not_139_out, not_140_out, not_141_out,
       not_142_out, not_143_out, not_144_out, not_145_out, not_146_out, not_147_out, not_148_out,
       not_149_out, not_150_out, not_151_out, not_152_out, not_153_out, not_154_out, not_155_out,
       not_156_out, not_157_out, not_158_out, not_159_out, not_160_out, not_161_out, not_162_out,
       not_163_out, not_164_out, not_165_out, not_166_out, not_167_out, not_168_out, not_169_out,
       not_170_out, not_171_out, not_172_out, not_173_out, not_174_out, not_175_out, not_176_out,
       not_177_out, not_178_out, not_179_out, not_180_out, not_181_out, not_182_out, not_183_out,
       not_184_out, not_185_out, not_186_out, not_187_out, not_188_out, not_189_out, not_190_out,
       not_191_out, not_192_out, not_193_out, not_194_out, not_195_out, not_196_out, not_197_out,
       not_198_out, not_199_out, not_200_out, not_201_out, not_202_out, not_203_out, not_204_out,
       not_205_out, not_206_out, not_207_out, not_208_out, not_209_out, not_210_out, not_211_out,
       not_212_out, not_213_out, not_214_out, not_215_out, not_216_out, not_217_out, not_218_out,
       not_219_out, not_220_out, not_221_out, not_222_out, not_223_out, not_224_out, not_225_out,
       not_226_out, not_227_out, not_228_out, not_229_out, not_230_out, not_231_out, not_232_out,
       not_233_out, not_234_out, not_235_out, not_236_out, not_237_out, not_238_out, not_239_out;

  not not_1 (not_1_out, I31);
  not not_2 (not_2_out, I30);
  not not_3 (not_3_out, I28);
  not not_4 (not_4_out, I27);
  not not_5 (not_5_out, I26);
  not not_6 (not_6_out, I4);
  not not_7 (not_7_out, I3);
  not not_8 (not_8_out, I2);
  not not_9 (not_9_out, I1);
  not not_10 (not_10_out, I0);
  not not_11 (not_11_out, I31);
  not not_12 (not_12_out, I30);
  not not_13 (not_13_out, I28);
  not not_14 (not_14_out, I27);
  not not_15 (not_15_out, I26);
  not not_16 (not_16_out, I4);
  not not_17 (not_17_out, I3);
  not not_18 (not_18_out, I1);
  not not_19 (not_19_out, I31);
  not not_20 (not_20_out, I30);
  not not_21 (not_21_out, I29);
  not not_22 (not_22_out, I28);
  not not_23 (not_23_out, I27);
  not not_24 (not_24_out, I26);
  not not_25 (not_25_out, I5);
  not not_26 (not_26_out, I4);
  not not_27 (not_27_out, I3);
  not not_28 (not_28_out, I2);
  not not_29 (not_29_out, I1);
  not not_30 (not_30_out, I0);
  not not_31 (not_31_out, I31);
  not not_32 (not_32_out, I30);
  not not_33 (not_33_out, I29);
  not not_34 (not_34_out, I28);
  not not_35 (not_35_out, I27);
  not not_36 (not_36_out, I26);
  not not_37 (not_37_out, I5);
  not not_38 (not_38_out, I4);
  not not_39 (not_39_out, I3);
  not not_40 (not_40_out, I2);
  not not_41 (not_41_out, I0);
  not not_42 (not_42_out, I31);
  not not_43 (not_43_out, I30);
  not not_44 (not_44_out, I28);
  not not_45 (not_45_out, I27);
  not not_46 (not_46_out, I26);
  not not_47 (not_47_out, I31);
  not not_48 (not_48_out, I30);
  not not_49 (not_49_out, I27);
  not not_50 (not_50_out, I30);
  not not_51 (not_51_out, I28);
  not not_52 (not_52_out, I31);
  not not_53 (not_53_out, I30);
  not not_54 (not_54_out, I29);
  not not_55 (not_55_out, I28);
  not not_56 (not_56_out, I27);
  not not_57 (not_57_out, I26);
  not not_58 (not_58_out, I4);
  not not_59 (not_59_out, I3);
  not not_60 (not_60_out, I1);
  not not_61 (not_61_out, I0);
  not not_62 (not_62_out, I31);
  not not_63 (not_63_out, I30);
  not not_64 (not_64_out, I29);
  not not_65 (not_65_out, I28);
  not not_66 (not_66_out, I27);
  not not_67 (not_67_out, I26);
  not not_68 (not_68_out, I4);
  not not_69 (not_69_out, I3);
  not not_70 (not_70_out, I31);
  not not_71 (not_71_out, I30);
  not not_72 (not_72_out, I29);
  not not_73 (not_73_out, I28);
  not not_74 (not_74_out, I27);
  not not_75 (not_75_out, I26);
  not not_76 (not_76_out, I5);
  not not_77 (not_77_out, I4);
  not not_78 (not_78_out, I3);
  not not_79 (not_79_out, I2);
  not not_80 (not_80_out, I1);
  not not_81 (not_81_out, I0);
  not not_82 (not_82_out, I31);
  not not_83 (not_83_out, I30);
  not not_84 (not_84_out, I29);
  not not_85 (not_85_out, I28);
  not not_86 (not_86_out, I27);
  not not_87 (not_87_out, I26);
  not not_88 (not_88_out, I5);
  not not_89 (not_89_out, I4);
  not not_90 (not_90_out, I3);
  not not_91 (not_91_out, I2);
  not not_92 (not_92_out, I0);
  not not_93 (not_93_out, I31);
  not not_94 (not_94_out, I30);
  not not_95 (not_95_out, I27);
  not not_96 (not_96_out, I26);
  not not_97 (not_97_out, I31);
  not not_98 (not_98_out, I30);
  not not_99 (not_99_out, I29);
  not not_100 (not_100_out, I27);
  not not_101 (not_101_out, I26);
  not not_102 (not_102_out, I4);
  not not_103 (not_103_out, I3);
  not not_104 (not_104_out, I2);
  not not_105 (not_105_out, I0);
  not not_106 (not_106_out, I31);
  not not_107 (not_107_out, I30);
  not not_108 (not_108_out, I29);
  not not_109 (not_109_out, I27);
  not not_110 (not_110_out, I26);
  not not_111 (not_111_out, I4);
  not not_112 (not_112_out, I3);
  not not_113 (not_113_out, I1);
  not not_114 (not_114_out, I31);
  not not_115 (not_115_out, I30);
  not not_116 (not_116_out, I29);
  not not_117 (not_117_out, I28);
  not not_118 (not_118_out, I27);
  not not_119 (not_119_out, I26);
  not not_120 (not_120_out, I5);
  not not_121 (not_121_out, I4);
  not not_122 (not_122_out, I3);
  not not_123 (not_123_out, I2);
  not not_124 (not_124_out, I0);
  not not_125 (not_125_out, I31);
  not not_126 (not_126_out, I30);
  not not_127 (not_127_out, I27);
  not not_128 (not_128_out, I26);
  not not_129 (not_129_out, I31);
  not not_130 (not_130_out, I30);
  not not_131 (not_131_out, I27);
  not not_132 (not_132_out, I31);
  not not_133 (not_133_out, I30);
  not not_134 (not_134_out, I29);
  not not_135 (not_135_out, I28);
  not not_136 (not_136_out, I27);
  not not_137 (not_137_out, I26);
  not not_138 (not_138_out, I31);
  not not_139 (not_139_out, I30);
  not not_140 (not_140_out, I29);
  not not_141 (not_141_out, I28);
  not not_142 (not_142_out, I31);
  not not_143 (not_143_out, I30);
  not not_144 (not_144_out, I29);
  not not_145 (not_145_out, I27);
  not not_146 (not_146_out, I26);
  not not_147 (not_147_out, I30);
  not not_148 (not_148_out, I29);
  not not_149 (not_149_out, I28);
  not not_150 (not_150_out, I30);
  not not_151 (not_151_out, I28);
  not not_152 (not_152_out, I31);
  not not_153 (not_153_out, I30);
  not not_154 (not_154_out, I27);
  not not_155 (not_155_out, I26);
  not not_156 (not_156_out, I31);
  not not_157 (not_157_out, I30);
  not not_158 (not_158_out, I27);
  not not_159 (not_159_out, I30);
  not not_160 (not_160_out, I28);
  not not_161 (not_161_out, I31);
  not not_162 (not_162_out, I30);
  not not_163 (not_163_out, I28);
  not not_164 (not_164_out, I27);
  not not_165 (not_165_out, I26);
  not not_166 (not_166_out, I3);
  not not_167 (not_167_out, I31);
  not not_168 (not_168_out, I30);
  not not_169 (not_169_out, I28);
  not not_170 (not_170_out, I27);
  not not_171 (not_171_out, I26);
  not not_172 (not_172_out, I31);
  not not_173 (not_173_out, I30);
  not not_174 (not_174_out, I28);
  not not_175 (not_175_out, I27);
  not not_176 (not_176_out, I26);
  not not_177 (not_177_out, I31);
  not not_178 (not_178_out, I30);
  not not_179 (not_179_out, I28);
  not not_180 (not_180_out, I27);
  not not_181 (not_181_out, I26);
  not not_182 (not_182_out, I31);
  not not_183 (not_183_out, I30);
  not not_184 (not_184_out, I28);
  not not_185 (not_185_out, I27);
  not not_186 (not_186_out, I26);
  not not_187 (not_187_out, I31);
  not not_188 (not_188_out, I30);
  not not_189 (not_189_out, I28);
  not not_190 (not_190_out, I27);
  not not_191 (not_191_out, I26);
  not not_192 (not_192_out, I30);
  not not_193 (not_193_out, I29);
  not not_194 (not_194_out, I28);
  not not_195 (not_195_out, I31);
  not not_196 (not_196_out, I30);
  not not_197 (not_197_out, I27);
  not not_198 (not_198_out, I26);
  not not_199 (not_199_out, I31);
  not not_200 (not_200_out, I30);
  not not_201 (not_201_out, I27);
  not not_202 (not_202_out, I31);
  not not_203 (not_203_out, I30);
  not not_204 (not_204_out, I29);
  not not_205 (not_205_out, I28);
  not not_206 (not_206_out, I27);
  not not_207 (not_207_out, I26);
  not not_208 (not_208_out, I5);
  not not_209 (not_209_out, I4);
  not not_210 (not_210_out, I3);
  not not_211 (not_211_out, I2);
  not not_212 (not_212_out, I1);
  not not_213 (not_213_out, I0);
  not not_214 (not_214_out, I31);
  not not_215 (not_215_out, I30);
  not not_216 (not_216_out, I29);
  not not_217 (not_217_out, I28);
  not not_218 (not_218_out, I27);
  not not_219 (not_219_out, I26);
  not not_220 (not_220_out, I5);
  not not_221 (not_221_out, I4);
  not not_222 (not_222_out, I3);
  not not_223 (not_223_out, I2);
  not not_224 (not_224_out, I0);
  not not_225 (not_225_out, I31);
  not not_226 (not_226_out, I30);
  not not_227 (not_227_out, I29);
  not not_228 (not_228_out, I28);
  not not_229 (not_229_out, I27);
  not not_230 (not_230_out, I26);
  not not_231 (not_231_out, I5);
  not not_232 (not_232_out, I4);
  not not_233 (not_233_out, I2);
  not not_234 (not_234_out, I1);
  not not_235 (not_235_out, I0);
  not not_236 (not_236_out, I31);
  not not_237 (not_237_out, I30);
  not not_238 (not_238_out, I29);
  not not_239 (not_239_out, I28);
  and and_1 (and_1_out, not_1_out, not_2_out, not_3_out, not_4_out, not_5_out, I5, not_6_out, not_7_out, not_8_out, not_9_out, not_10_out);
  and and_2 (and_2_out, not_11_out, not_12_out, not_13_out, not_14_out, not_15_out, I5, not_16_out, not_17_out, I2, not_18_out, I0);
  and and_3 (and_3_out, not_19_out, not_20_out, not_21_out, not_22_out, not_23_out, not_24_out, not_25_out, not_26_out, not_27_out, not_28_out, not_29_out, not_30_out);
  and and_4 (and_4_out, not_31_out, not_32_out, not_33_out, not_34_out, not_35_out, not_36_out, not_37_out, not_38_out, not_39_out, not_40_out, I1, not_41_out);
  and and_5 (and_5_out, not_42_out, not_43_out, I29, not_44_out, not_45_out, not_46_out);
  and and_6 (and_6_out, not_47_out, not_48_out, I29, I28, not_49_out, I26);
  and and_7 (and_7_out, I31, not_50_out, not_51_out, I27, I26);
  and and_8 (and_8_out, not_52_out, not_53_out, not_54_out, not_55_out, not_56_out, not_57_out, I5, not_58_out, not_59_out, I2, not_60_out, not_61_out);
  and and_9 (and_9_out, not_62_out, not_63_out, not_64_out, not_65_out, not_66_out, not_67_out, I5, not_68_out, not_69_out, I2, I1, I0);
  and and_10 (and_10_out, not_70_out, not_71_out, not_72_out, not_73_out, not_74_out, not_75_out, not_76_out, not_77_out, not_78_out, not_79_out, not_80_out, not_81_out);
  and and_11 (and_11_out, not_82_out, not_83_out, not_84_out, not_85_out, not_86_out, not_87_out, not_88_out, not_89_out, not_90_out, not_91_out, I1, not_92_out);
  and and_12 (and_12_out, not_93_out, not_94_out, I29, I28, not_95_out, not_96_out);
  and and_13 (and_13_out, not_97_out, not_98_out, not_99_out, not_100_out, not_101_out, I5, not_102_out, not_103_out, not_104_out, I1, not_105_out);
  and and_14 (and_14_out, not_106_out, not_107_out, not_108_out, not_109_out, not_110_out, I5, not_111_out, not_112_out, I2, not_113_out);
  and and_15 (and_15_out, not_114_out, not_115_out, not_116_out, not_117_out, not_118_out, not_119_out, not_120_out, not_121_out, not_122_out, not_123_out, I1, not_124_out);
  and and_16 (and_16_out, not_125_out, not_126_out, I28, not_127_out, not_128_out);
  and and_17 (and_17_out, not_129_out, not_130_out, I29, I28, not_131_out);
  and and_18 (RegDst, not_132_out, not_133_out, not_134_out, not_135_out, not_136_out, not_137_out);
  and and_19 (Jump, not_138_out, not_139_out, not_140_out, not_141_out, I27);
  and and_20 (Branch, not_142_out, not_143_out, not_144_out, I28, not_145_out, not_146_out);
  and and_21 (MemRead, I31, not_147_out, not_148_out, not_149_out, I27, I26);
  and and_22 (MemWrite, I31, not_150_out, I29, not_151_out, I27, I26);
  and and_23 (and_23_out, not_152_out, not_153_out, I29, not_154_out, not_155_out);
  or or_1 (ALUSrc, and_23_out, and_24_out, and_25_out);
  and and_24 (and_24_out, not_156_out, not_157_out, I29, I28, not_158_out);
  and and_25 (and_25_out, I31, not_159_out, not_160_out, I27, I26);
  and and_26 (and_26_out, not_161_out, not_162_out, not_163_out, not_164_out, not_165_out, not_166_out);
  and and_27 (and_27_out, not_167_out, not_168_out, not_169_out, not_170_out, not_171_out, I0);
  and and_28 (and_28_out, not_172_out, not_173_out, not_174_out, not_175_out, not_176_out, I1);
  and and_29 (and_29_out, not_177_out, not_178_out, not_179_out, not_180_out, not_181_out, I2);
  and and_30 (and_30_out, not_182_out, not_183_out, not_184_out, not_185_out, not_186_out, I4);
  and and_31 (and_31_out, not_187_out, not_188_out, not_189_out, not_190_out, not_191_out, I5);
  and and_32 (and_32_out, not_192_out, not_193_out, not_194_out, I27, I26);
  and and_33 (and_33_out, not_195_out, not_196_out, I29, not_197_out, not_198_out);
  and and_34 (and_34_out, not_199_out, not_200_out, I29, I28, not_201_out);
  and and_35 (and_35_out, not_202_out, not_203_out, not_204_out, not_205_out, not_206_out, not_207_out, not_208_out, not_209_out, not_210_out, not_211_out, not_212_out, not_213_out);
  and and_36 (and_36_out, not_214_out, not_215_out, not_216_out, not_217_out, not_218_out, not_219_out, not_220_out, not_221_out, not_222_out, not_223_out, I1, not_224_out);
  and and_37 (Jr, not_225_out, not_226_out, not_227_out, not_228_out, not_229_out, not_230_out, not_231_out, not_232_out, I3, not_233_out, not_234_out, not_235_out);
  and and_38 (Jal, not_236_out, not_237_out, not_238_out, not_239_out, I27, I26);
  or or_2 (ALU2, and_1_out, and_2_out, and_3_out, and_4_out, and_5_out, and_6_out, and_7_out);
  or or_3 (ALU1, and_8_out, and_9_out, and_10_out, and_11_out, and_12_out);
  or or_4 (ALU0, and_13_out, and_14_out, and_15_out, and_16_out, and_17_out);
  or or_5 (RegWrite, and_26_out, and_27_out, and_28_out, and_29_out, and_30_out, and_31_out, and_32_out, and_33_out, and_34_out, and_35_out, and_36_out);

  assign MemToReg = MemRead;

  // Notes on the sheet:
  //   MemRead and MemToReg are connected because they emit the same signals anyways.
endmodule
